// Logisim project main.circ as structural Verilog: 1 circuit, main circuit main
module main (
  input  R,
  input  S,
  input  S_2,
  input  R_2,
  input  S_3,
  input  in_6,
  input  in_7,
  input  _4,
  input  in_9,
  input  in_10,
  input  in_11,
  input  in_12,
  input  in_13,
  output Q,
  output notQ,
  output Q_2,
  output notQ_2,
  output out_18,
  output out_19,
  output out_20,
  output out_21,
  output out_22,
  output out_23,
  output out_24,
  output out_25
);

  wire nand_3_out, nand_4_out, nand_5_out, nand_6_out, nand_7_out, nand_8_out, nand_9_out, nand_10_out,
       nand_17_out, nand_18_out;

  nand nand_1 (Q_2, S_2, notQ_2);
  nand nand_2 (notQ_2, Q_2, R_2);
  nand nand_3 (nand_3_out, S_3, in_6);
  nand nand_4 (nand_4_out, in_6, in_7);
  nand nand_5 (nand_5_out, _4, _4);
  nand nand_6 (nand_6_out, nand_5_out, in_9);
  nand nand_7 (nand_7_out, in_10, nand_8_out);
  nand nand_8 (nand_8_out, in_11, in_11);
  nand nand_9 (nand_9_out, in_12, in_12);
  nand nand_10 (nand_10_out, in_13, in_13);
  nor nor_1 (Q, R, notQ);
  nor nor_2 (notQ, Q, S);
  nand nand_11 (out_18, nand_3_out, out_19);
  nand nand_12 (out_19, out_18, nand_4_out);
  nand nand_13 (out_20, nand_5_out, out_21);
  nand nand_14 (out_21, out_20, nand_6_out);
  nand nand_15 (out_22, nand_7_out, out_23);
  nand nand_16 (out_23, out_22, nand_8_out);
  nand nand_17 (nand_17_out, nand_10_out, in_12);
  nand nand_18 (nand_18_out, nand_9_out, in_13);
  nand nand_19 (out_24, nand_17_out, out_25);
  nand nand_20 (out_25, out_24, nand_18_out);

  // Notes on the sheet:
  //   1
  //   2
  //   3
  //   5
  //   6
endmodule
