// Logisim project main.circ as structural Verilog: 1 circuit, main circuit main
module main (
  input  in_1,
  input  in_2,
  input  in_3,
  input  \D_триггер ,
  input  in_5,
  output out_6,
  output out_7,
  output out_8,
  output out_9
);

  wire nand_1_out, nand_2_out, nand_3_out, nand_4_out, nand_7_out, nand_8_out, nand_9_out, nand_10_out;

  nand nand_1 (nand_1_out, out_7, in_1, in_2);
  nand nand_2 (nand_2_out, in_2, in_3, out_6);
  nand nand_3 (nand_3_out, \D_триггер , in_5);
  nand nand_4 (nand_4_out, nand_3_out, in_5);
  nand nand_5 (out_8, nand_3_out, out_9);
  nand nand_6 (out_9, out_8, nand_4_out);
  nand nand_7 (nand_7_out, nand_1_out, nand_8_out);
  nand nand_8 (nand_8_out, nand_7_out, nand_2_out);
  nand nand_9 (nand_9_out, nand_1_out, nand_7_out);
  nand nand_10 (nand_10_out, nand_8_out, nand_2_out);
  nand nand_11 (out_6, nand_9_out, out_7);
  nand nand_12 (out_7, out_6, nand_10_out);

  // Notes on the sheet:
  //   jk-триггер
endmodule
