// Logisim project main.circ as structural Verilog
module \Сравнитор  (
  input  in_1,
  input  in_2,
  output out_3
);

  wire and_1_out, and_2_out, not_1_out, not_2_out;

  not not_1 (not_1_out, in_1);
  not not_2 (not_2_out, in_2);
  and and_1 (and_1_out, not_1_out, in_2);
  and and_2 (and_2_out, in_1, not_2_out, not_2_out);
  or or_1 (out_3, and_1_out, and_2_out);
endmodule

module \Полусумматор  (
  input  in_1,
  input  in_2,
  output out_3,
  output out_4
);

  \Сравнитор  \u_сравнитор_1  (.in_1(in_1), .in_2(in_2), .out_3(out_4));
  and and_1 (out_3, in_1, in_2);
endmodule

module \Сумматор  (
  input  in_1,
  input  in_2,
  input  in_3,
  output out_4,
  output out_5
);

  wire \полусумматор_1_out_3 , \полусумматор_1_out_4 , \полусумматор_2_out_3 ;

  \Полусумматор  \u_полусумматор_1  (
    .in_1(in_1), .in_2(in_2), .out_3(\полусумматор_1_out_3 ), .out_4(\полусумматор_1_out_4 ));
  \Полусумматор  \u_полусумматор_2  (
    .in_1(\полусумматор_1_out_4 ), .in_2(in_3), .out_3(\полусумматор_2_out_3 ), .out_4(out_5));
  or or_1 (out_4, \полусумматор_1_out_3 , \полусумматор_2_out_3 );
endmodule

module \_4х_Сумматор  (
  input  X1,
  input  X2,
  input  X3,
  input  X4,
  input  Y1,
  input  Y2,
  input  Y3,
  input  Y4,
  input  P0,
  output S1,
  output S2,
  output S3,
  output S4,
  output S5
);

  wire \сумматор_1_out_4 , \сумматор_2_out_4 , \сумматор_3_out_4 ;

  \Сумматор  \u_сумматор_1  (.in_1(Y1), .in_2(X1), .in_3(P0), .out_4(\сумматор_1_out_4 ), .out_5(S1));
  \Сумматор  \u_сумматор_2  (.in_1(Y2), .in_2(X2), .in_3(\сумматор_1_out_4 ), .out_4(\сумматор_2_out_4 ), .out_5(S2));
  \Сумматор  \u_сумматор_3  (.in_1(Y3), .in_2(X3), .in_3(\сумматор_2_out_4 ), .out_4(\сумматор_3_out_4 ), .out_5(S3));
  \Сумматор  \u_сумматор_4  (.in_1(Y4), .in_2(X4), .in_3(\сумматор_3_out_4 ), .out_4(S5), .out_5(S4));
endmodule

module \Полный_одноразрядный_сумматор  (
  input  A,
  input  B,
  output S,
  output P
);

  wire not_1_out, or_1_out;

  or or_1 (or_1_out, A, B);
  and and_1 (P, A, B);
  not not_1 (not_1_out, P);
  and and_2 (S, or_1_out, not_1_out);
endmodule

module \Двоичный_сумматор  (
  input  A,
  input  B,
  input  P0,
  output P,
  output S
);

  wire and_1_out, and_2_out, and_3_out, and_4_out, and_5_out, not_1_out, or_1_out;

  and and_1 (and_1_out, A, B);
  and and_2 (and_2_out, A, P0);
  and and_3 (and_3_out, B, P0);
  or or_1 (or_1_out, A, B, P0);
  and and_4 (and_4_out, A, B, P0);
  or or_2 (P, and_1_out, and_2_out, and_3_out);
  not not_1 (not_1_out, P);
  and and_5 (and_5_out, not_1_out, or_1_out);
  or or_3 (S, and_5_out, and_4_out);
endmodule
